# Fritzing sketch SESH_Tester1 (saved by Fritzing 0.9.3b)
breadboards: 1

parts:
  IC1 = MCP3008 8-channel 10-bit ADC [part_number=MCP3008]
  Raspberry_Pi_1 = Raspberry Pi 3 [part_number=RPI-3-V1.2]
  R1 = Trimmer Potentiometer [maximum_resistance=10kΩ package=THT]
  R2 = Trimmer Potentiometer [maximum_resistance=10kΩ package=THT]
  LED2 = LED - 5mm [color="Red (633nm)" package="5 mm [THT]"]  # not connected
  R3 = Resistor [tolerance=±5% resistance=220 package="0402 [SMD]"]
  LED3 = LED - 5mm [color="Red (633nm)" package="5 mm [THT]"]
  R4 = Resistor [tolerance=±5% resistance=220 package="0805 [SMD]"]

nets:
  N1: IC1.no_name_yet#7, R2.wiper
  N2: IC1.no_name_yet#8, R1.wiper
  N3: IC1.no_name_yet#9, IC1.no_name_yet#14, Raspberry_Pi_1.GND, R1.leg2, R2.leg2, LED3.cathode
  N4: IC1.no_name_yet#10, Raspberry_Pi_1.GPIO8
  N5: IC1.no_name_yet#11, Raspberry_Pi_1.GPIO10
  N6: IC1.no_name_yet#12, Raspberry_Pi_1.GPIO9
  N7: IC1.no_name_yet#13, Raspberry_Pi_1.GPIO11
  N8: IC1.no_name_yet#15, IC1.no_name_yet#16, Raspberry_Pi_1.3v3, R1.leg1, R2.leg1
  N9: Raspberry_Pi_1.GPIO21, R3.Pin_0
  N10: Raspberry_Pi_1.GPIO20, R4.Pin_0
  N11: LED3.anode, R4.Pin_1
